# Fritzing sketch MG811_CO2_fritzing (saved by Fritzing 0.9.4)
breadboards: 1

parts:
  MG-811 = IC, SIP package, 3 pins [chip_label=MG-811]
  Argon1 = Particle Argon

nets:
  N1: MG-811.pin1, Argon1.A0
  N2: MG-811.pin2, Argon1.VUSB
  N3: MG-811.pin3, Argon1.GND

custom parts:
  Particle Argon: The Argon is a powerful Wi-Fi enabled development board that can act as either a standalone Wi-Fi endpoint or Wi-Fi enabled gateway for Particle Mesh networks. It is based on the Nordic nRF52840 and has built-in battery charging circuitry so it’s easy to connect a Li-Po and deploy your local network in minutes. The Argon is great for connecting existing projects to the Particle Device Cloud or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
