# Fritzing sketch MQ9_CO_fritzing (saved by Fritzing 0.9.4)
breadboards: 1

parts:
  ADC121C = SO08w [package=SO(w)]
  Argon1 = Particle Argon

nets:
  N1: ADC121C.1, Argon1.SCL
  N2: ADC121C.4, Argon1.VUSB
  N3: ADC121C.7, Argon1.GND
  N4: ADC121C.8, Argon1.SDA

custom parts:
  Particle Argon: The Argon is a powerful Wi-Fi enabled development board that can act as either a standalone Wi-Fi endpoint or Wi-Fi enabled gateway for Particle Mesh networks. It is based on the Nordic nRF52840 and has built-in battery charging circuitry so it’s easy to connect a Li-Po and deploy your local network in minutes. The Argon is great for connecting existing projects to the Particle Device Cloud or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
